# Fritzing sketch Sketch (saved by Fritzing 0.9.6b)
breadboards: 1

parts:
  Part1 = Adafruit T-Cobbler Plus [part_number="Adafruit #1989 and #2028"]
  D1 = LTE-302 [package=lte-302]
  R1 = Resistor [tolerance=±5% resistance=220 package="1206 [SMD]"]
  R2 = Resistor [tolerance=±5% resistance=220 package="1206 [SMD]"]
  D2 = LTE-302 [package=lte-302]

nets:
  N1: Part1.GND, R1.Pin_1, R2.Pin_1
  N2: Part1.GPIO20, D1.C
  N3: Part1.GPIO21, D2.C
  N4: D1.A, R1.Pin_0
  N5: R2.Pin_0, D2.A

custom parts:
  Adafruit T-Cobbler Plus: The Raspberry Pi has landed on the Maker World like a 40-GPIO pinned, quad-USB ported, credit card sized bomb of DIY joy. And while you can use most of our great Model B accessories by hooking up our downgrade cable, its probably a good time to upgrade your set up and accessorize using all of the 40 pins. That's why we now carry the Assembled Adafruit Pi T-Cobbler Plus - Breakout + Cable for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
